// Logisim project Guia_0401.circ as structural Verilog: 1 circuit, main circuit main
module main (
  input  x,
  input  y,
  input  z,
  output _1a,
  output _1b,
  output _1c,
  output _1d,
  output _1e
);

  wire and_1_out, and_2_out, not_1_out, not_2_out, not_3_out, not_4_out, not_5_out, not_6_out, not_7_out,
       not_8_out, not_9_out, not_10_out, not_11_out, not_12_out, or_1_out, or_2_out, or_3_out, or_4_out;

  or or_1 (or_1_out, y, not_1_out);
  not not_1 (not_1_out, z);
  not not_2 (not_2_out, y);
  or or_2 (or_2_out, not_2_out, x);
  not not_3 (not_3_out, x);
  and and_1 (and_1_out, not_3_out, y);
  not not_4 (not_4_out, z);
  not not_5 (not_5_out, x);
  and and_2 (and_2_out, not_5_out, not_6_out);
  not not_6 (not_6_out, y);
  or or_3 (or_3_out, x, y);
  not not_7 (not_7_out, y);
  or or_4 (or_4_out, not_7_out, z);
  not not_8 (not_8_out, or_1_out);
  not not_9 (not_9_out, or_2_out);
  and and_3 (_1b, not_9_out, z);
  not not_10 (not_10_out, and_1_out);
  and and_4 (_1c, not_10_out, not_4_out);
  not not_11 (not_11_out, and_2_out);
  not not_12 (not_12_out, or_4_out);
  and and_5 (_1a, not_8_out, x);
  and and_6 (_1d, not_11_out, z);
  and and_7 (_1e, or_3_out, not_12_out);

  // Notes on the sheet:
  //   806454 - Yago Almeida Melo
endmodule
