// Logisim project Guia_0601.circ as structural Verilog: 1 circuit, main circuit main
module main (
  input  x,
  input  y,
  input  z,
  input  x_2,
  input  y_2,
  input  z_2,
  input  x_3,
  input  y_3,
  input  z_3,
  input  x_4,
  input  y_4,
  input  z_4,
  input  x_5,
  input  y_5,
  input  z_5,
  output out_16,
  output out_17,
  output out_18,
  output out_19
);

  wire and_1_out, and_2_out, and_3_out, and_4_out, and_5_out, and_6_out, and_7_out, and_8_out, and_9_out,
       and_10_out, not_1_out, not_2_out, not_3_out, not_4_out, not_5_out, not_6_out, not_7_out, not_8_out,
       not_9_out, not_10_out, not_11_out, not_12_out, not_13_out, not_14_out, not_15_out, or_1_out;

  not not_1 (not_1_out, x);
  not not_2 (not_2_out, x_2);
  not not_3 (not_3_out, x_3);
  not not_4 (not_4_out, x_4);
  not not_5 (not_5_out, y);
  not not_6 (not_6_out, y_2);
  not not_7 (not_7_out, y_3);
  not not_8 (not_8_out, y_4);
  not not_9 (not_9_out, y_5);
  not not_10 (not_10_out, x_5);
  not not_11 (not_11_out, z);
  not not_12 (not_12_out, z_2);
  not not_13 (not_13_out, z_3);
  not not_14 (not_14_out, z_4);
  not not_15 (not_15_out, z_5);
  and and_1 (and_1_out, not_1_out, z);
  and and_2 (and_2_out, y, z);
  and and_3 (and_3_out, not_2_out, not_12_out);
  and and_4 (and_4_out, y_2, not_12_out);
  and and_5 (and_5_out, y_3, not_13_out);
  and and_6 (and_6_out, x_3, not_7_out);
  and and_7 (and_7_out, not_8_out, z_4);
  and and_8 (and_8_out, not_4_out, y_4);
  and and_9 (and_9_out, not_9_out, not_15_out);
  and and_10 (and_10_out, x_5, z_5);
  or or_1 (or_1_out, and_1_out, and_2_out);
  or or_2 (out_16, and_3_out, and_4_out);
  or or_3 (out_17, and_5_out, and_6_out);
  or or_4 (out_18, and_7_out, and_8_out);
  or or_5 (out_19, and_9_out, and_10_out);

  // Notes on the sheet:
  //   Guia 0601$806454 - Yago Almeida Melo
endmodule
