// Logisim project Guia_0802.circ as structural Verilog: 1 circuit, main circuit main
module main (
  input  A,
  input  B,
  input  VIN,
  output out_4,
  output out_5
);

  wire and_1_out, and_2_out, and_3_out, xor_1_out;

  xor xor_1 (xor_1_out, A, B);
  and and_1 (and_1_out, ~A, VIN);  // AND_Gate
  and and_2 (and_2_out, ~A, B);  // AND_Gate
  and and_3 (and_3_out, ~B, VIN);  // AND_Gate
  xor xor_2 (out_4, xor_1_out, VIN);
  or or_1 (out_5, and_1_out, and_2_out, and_3_out);

  // Notes on the sheet:
  //   Guia_0802
  //   806454 - Yago Almeida Melo
endmodule
