// Logisim project Guia_0804.circ as structural Verilog: 1 circuit, main circuit main
module main (
  input  A1,
  input  A2,
  input  A3,
  input  A4,
  input  A5,
  input  A6,
  input  B1,
  input  B2,
  input  B3,
  input  B4,
  input  B5,
  input  B6,
  output out_13
);

  wire and_1_out, and_2_out, and_3_out, xnor_1_out, xnor_2_out, xnor_3_out, xnor_4_out, xnor_5_out,
       xnor_6_out;

  xnor xnor_1 (xnor_1_out, A1, B1);
  xnor xnor_2 (xnor_2_out, A2, B2);
  xnor xnor_3 (xnor_3_out, A3, B3);
  xnor xnor_4 (xnor_4_out, A4, B4);
  xnor xnor_5 (xnor_5_out, A5, B5);
  xnor xnor_6 (xnor_6_out, A6, B6);
  and and_1 (and_1_out, xnor_1_out, xnor_2_out);
  and and_2 (and_2_out, xnor_3_out, xnor_4_out);
  and and_3 (and_3_out, xnor_5_out, xnor_6_out);
  and and_4 (out_13, and_1_out, and_2_out, and_3_out);

  // Notes on the sheet:
  //   Guia_0804
  //   806454 - Yago Almeida Melo
endmodule
